// Digital circuit CacheSetAssoc2Way2WPB.dig as structural Verilog
module CacheSetAssoc2Way2WPB (
  input  [31:0] in_1,
  output out_2,
  output [31:0] out_3
);

  wire mvalid0, mvalid1;
  wire [8:0] controller_2w_2vias_1_index;
  wire [19:0] mtag0, mtag1;
  wire [31:0] data0, data1, word0, word1;

  controller_2w_2vias controller_2w_2vias_1 (
    .address(in_1), .mtag0(mtag0), .mtag1(mtag1), .data0(data0), .data1(data1), .mvalid0(mvalid0),
    .mvalid1(mvalid1), .mword1(word0), .mword0(word1), .index(controller_2w_2vias_1_index), .hit(out_2),
    .data(out_3));
  CacheSaMwMemory #(.applicationType("IVERILOG")) u_CacheSaMwMemory (
    .addr(controller_2w_2vias_1_index), .w0valid(mvalid0), .w0tag(mtag0), .w0word0(data0), .w0word1(data1),
    .w1valid(mvalid1), .w1tag(mtag1), .w1word0(word0), .w1word1(word1));

  // Other names for the same wires on the sheet: data[31:0] = out_3; hit = out_2
endmodule

/* Code of CacheSaMwMemory:
module CacheSaMwMemory(
    input [8:0] addr,
    output w0valid,
    output [19:0] w0tag,
    output [31:0] w0word0,
    output [31:0] w0word1,
    output w1valid,
    output [19:0] w1tag,
    output [31:0] w1word0,
    output [31:0] w1word1
);

    reg [169:0] memory [0:511];    
    wire [169:0] data;
    
    assign data = memory[addr];
    
    assign w0valid = data[169];
    assign w1valid = data[168];
    assign w0tag = data[167:148];
    assign w1tag = data[147:128];
    
    assign w0word0 = data[127:96];
    assign w0word1 = data[95:64];
    assign w1word0 = data[63:32];
    assign w1word1 = data[31:0];
    
    initial
    begin
        memory[1] = 170'h3_00000_00001_000000e7_000000e8_000000a7_000000a8;
    end
    
endmodule
*/
