// Digital circuit controller_2w_2vias.dig as structural Verilog
module controller_2w_2vias (
  input  [31:0] address,
  input  [19:0] mtag0,
  input  [19:0] mtag1,
  input  [31:0] data0,
  input  [31:0] data1,
  input  mvalid0,
  input  mvalid1,
  input  [31:0] mword1,
  input  [31:0] mword0,
  output [8:0] index,
  output hit,
  output [31:0] data
);

  wire and1, and2, c1, c2, p;
  wire [31:0] multiplexer_1_out, multiplexer_2_out;

  and and_1 (and1, c1, mvalid0);
  and and_2 (and2, c2, mvalid1);
  Comparator #(.Bits(20)) comparator_1 (.a(address[31:12]), .b(mtag0), .eq(c1));  // open: gt, lt
  Comparator #(.Bits(20)) comparator_2 (.a(address[31:12]), .b(mtag1), .eq(c2));  // open: gt, lt
  or or_1 (hit, and1, and2);
  PriorityEncoder priorityencoder_1 (.in0(and1), .in1(and2), .num(p));  // open: any
  Multiplexer #(.Bits(32)) multiplexer_1 (.sel(address[2]), .in_0(data0), .in_1(mword0), .out(multiplexer_1_out));
  Multiplexer #(.Bits(32)) multiplexer_2 (.sel(address[2]), .in_0(data1), .in_1(mword1), .out(multiplexer_2_out));
  Multiplexer #(.Bits(32)) multiplexer_3 (.sel(p), .in_0(multiplexer_1_out), .in_1(multiplexer_2_out), .out(data));

  assign index = address[11:3];

  // Other names for the same wires on the sheet: word_offset = address[2]; tag[19:0] = address[31:12];
  //   d0[31:0] = data0; d1[31:0] = data1; mt0[19:0] = mtag0; mt1[19:0] = mtag1
endmodule
