// Digital circuit CacheSetAssoc2Way2WPB.dig as structural Verilog
module CacheSetAssoc2Way2WPB (
  input  [31:0] in_1,
  output out_2,
  output [19:0] out_3,
  output [31:0] out_4,
  output [31:0] out_5,
  output out_6,
  output [19:0] out_7,
  output [31:0] out_8,
  output [31:0] out_9
);

  CacheSaMwMemory #(.applicationType("IVERILOG")) u_CacheSaMwMemory (
    .addr(in_1[11:3]), .w0valid(out_2), .w0tag(out_3), .w0word0(out_4), .w0word1(out_5), .w1valid(out_6),
    .w1tag(out_7), .w1word0(out_8), .w1word1(out_9));
endmodule

/* Code of CacheSaMwMemory:
module CacheSaMwMemory(
    input [8:0] addr,
    output w0valid,
    output [19:0] w0tag,
    output [31:0] w0word0,
    output [31:0] w0word1,
    output w1valid,
    output [19:0] w1tag,
    output [31:0] w1word0,
    output [31:0] w1word1
);

    reg [169:0] memory [0:511];    
    wire [169:0] data;
    
    assign data = memory[addr];
    
    assign w0valid = data[169];
    assign w1valid = data[168];
    assign w0tag = data[167:148];
    assign w1tag = data[147:128];
    
    assign w0word0 = data[127:96];
    assign w0word1 = data[95:64];
    assign w1word0 = data[63:32];
    assign w1word1 = data[31:0];
    
    initial
    begin
        memory[1] = 170'h3_00000_00001_000000e7_000000e8_000000a7_000000a8;
    end
    
endmodule
*/
